// Logisim project micro.circ as structural Verilog: 1 circuit, main circuit EV20_Superescalar
module EV20_Superescalar (
  input  in_1
);

  wire ALUALULAU_cyout, and_1_out, bloque1_1_preload, CLK, CLK2, CLK3, CLK4, dipswitch_1_sw1,
       LoadStore_kmx_out, not_1_out, not_2_out, not_3_out, pipeline_register_1_kmx_out,
       pipeline_register_2_kmx_out, UC1_ALU_EN, UC1_LS_EN, undriven, undriven_2;
  wire [1:0] LoadStore_mrymb_out, LoadStore_sh_out, pipeline_register_1_mrymb_out,
       pipeline_register_1_sh_out, pipeline_register_2_mrymb_out, pipeline_register_2_sh_out;
  wire [3:0] LoadStore_aluc_out, pipeline_register_1_aluc_out, pipeline_register_2_aluc_out;
  wire [4:0] LoadStore_a_bus_out, LoadStore_b_bus_out, pipeline_register_1_a_bus_out,
       pipeline_register_1_b_bus_out, pipeline_register_2_a_bus_out, pipeline_register_2_b_bus_out,
       selector_a_1_out_2;
  wire [5:0] LoadStore_c_bus_out, LoadStore_t_bus_out, pipeline_register_1_c_bus_out,
       pipeline_register_1_t_bus_out, pipeline_register_2_c_bus_out, pipeline_register_2_t_bus_out,
       selector_c_1_busc_selector;
  wire [9:0] LoadStore_d_address_out, pipeline_register_1_d_address_out, pipeline_register_2_d_address_out,
       UC1_ALU_DADRES, UC1_LS_DADRES;
  wire [10:0] ProgramCounterReg_ia0ia10;
  wire [14:0] MicroInstructionROM_microinstruction;
  wire [15:0] ALUALULAU_z, BusA_ALU_q, BusB_ALU_q;
  wire [23:0] BBUS, ProgramMemory_data;
  wire [30:0] pipeline_register_2_serial_out, UC1_ALU_SD, UC1_LS_SD;

  // Probe on ProgramCounterReg_ia0ia10
  ROM #(.addrWidth(11), .dataWidth(24)) ProgramMemory (.addr(ProgramCounterReg_ia0ia10), .data(ProgramMemory_data));
  Bloque1 bloque1_1 (.WRegister(16'hfff), .B12B11(BBUS[21:20]), .Preload(bloque1_1_preload));  // open: CY
  and and_1 (and_1_out, bloque1_1_preload, BBUS[22]);
  PCreg ProgramCounterReg (
    .Preload(and_1_out), .CLK1(CLK), .HOLD(undriven), .B0B10(BBUS[15:5]), .IA0IA10(ProgramCounterReg_ia0ia10));
  Register #(.width(24)) InstructionRegister (.D(ProgramMemory_data), .en(undriven), .clk(CLK), .Q(BBUS));  // open: clr
  // Probe on BBUS
  not not_1 (not_1_out, UC1_ALU_EN);
  Selector_A selector_a_1 (.BusB(BBUS), .out_2(selector_a_1_out_2));
  Pipeline_register pipeline_register_1 (
    .S_low_P_high(1'b0), .CLK(CLK3), .Serial_IN(UC1_ALU_SD), .D_Address_IN(UC1_ALU_DADRES), .Hold(not_1_out),
    .ALUC_OUT(pipeline_register_1_aluc_out), .SH_OUT(pipeline_register_1_sh_out),
    .Kmx_OUT(pipeline_register_1_kmx_out), .MRyMB_OUT(pipeline_register_1_mrymb_out),
    .B_bus_OUT(pipeline_register_1_b_bus_out), .T_bus_OUT(pipeline_register_1_t_bus_out),
    .C_bus_OUT(pipeline_register_1_c_bus_out), .A_bus_OUT(pipeline_register_1_a_bus_out),
    .D_Address_OUT(pipeline_register_1_d_address_out));  // open: ALUC_IN, SH_IN, Kmx_IN, MRyMB_IN, B_bus_IN, T_bus_IN, C_bus_IN, A_bus_IN, Serial_OUT
  // Probe on pipeline_register_1_sh_out
  // Probe on pipeline_register_1_kmx_out
  // Probe on pipeline_register_1_mrymb_out
  // Probe on pipeline_register_1_b_bus_out
  // Probe on pipeline_register_1_t_bus_out
  // Probe on pipeline_register_1_c_bus_out
  // Probe on pipeline_register_1_a_bus_out
  // Probe on pipeline_register_1_d_address_out
  Selector_C selector_c_1 (.BusB(BBUS), .BusC_Selector(selector_c_1_busc_selector));
  // Probe on pipeline_register_1_aluc_out
  Micro_Instruction_ROM MicroInstructionROM (
    .Instruction(BBUS), .MicroInstruction(MicroInstructionROM_microinstruction));
  Register #(.width(16)) BusA_ALU (.D(16'h1), .en(UC1_ALU_EN), .clk(CLK2), .Q(BusA_ALU_q));  // open: clr
  Register #(.width(16)) BusB_ALU (.D(16'h2), .en(UC1_ALU_EN), .clk(CLK2), .Q(BusB_ALU_q));  // open: clr
  not not_2 (not_2_out, undriven_2);
  // Probe on pipeline_register_2_aluc_out
  Pipeline_register pipeline_register_2 (
    .ALUC_IN(MicroInstructionROM_microinstruction[14:11]),
    .SH_IN(MicroInstructionROM_microinstruction[10:9]), .Kmx_IN(MicroInstructionROM_microinstruction[8]),
    .S_low_P_high(1'b1), .CLK(CLK2), .MRyMB_IN(MicroInstructionROM_microinstruction[7:6]),
    .B_bus_IN(BBUS[14:10]), .T_bus_IN(MicroInstructionROM_microinstruction[5:0]),
    .C_bus_IN(selector_c_1_busc_selector), .A_bus_IN(selector_a_1_out_2), .D_Address_IN(BBUS[14:5]),
    .ALUC_OUT(pipeline_register_2_aluc_out), .SH_OUT(pipeline_register_2_sh_out),
    .Kmx_OUT(pipeline_register_2_kmx_out), .MRyMB_OUT(pipeline_register_2_mrymb_out),
    .B_bus_OUT(pipeline_register_2_b_bus_out), .T_bus_OUT(pipeline_register_2_t_bus_out),
    .C_bus_OUT(pipeline_register_2_c_bus_out), .Serial_OUT(pipeline_register_2_serial_out),
    .A_bus_OUT(pipeline_register_2_a_bus_out), .D_Address_OUT(pipeline_register_2_d_address_out));  // open: Serial_IN, Hold
  // Probe on pipeline_register_2_sh_out
  // Probe on pipeline_register_2_kmx_out
  // Probe on pipeline_register_2_mrymb_out
  // Probe on pipeline_register_2_b_bus_out
  // Probe on pipeline_register_2_t_bus_out
  // Probe on pipeline_register_2_c_bus_out
  // Probe on pipeline_register_2_a_bus_out
  // Probe on ALUALULAU_z
  ALU ALUALULAU (
    .ALUC(pipeline_register_1_aluc_out), .A(BusA_ALU_q), .B(BusB_ALU_q), .Z(ALUALULAU_z),
    .CYout(ALUALULAU_cyout));  // open: CYin
  // Probe on ALUALULAU_cyout
  Pipeline_register pipeline_register_3 (
    .S_low_P_high(1'b0), .Hold(not_2_out));  // open: ALUC_IN, SH_IN, Kmx_IN, CLK, MRyMB_IN, B_bus_IN, T_bus_IN, C_bus_IN, Serial_IN, A_bus_IN, D_Address_IN, ALUC_OUT, SH_OUT, Kmx_OUT, MRyMB_OUT, B_bus_OUT, T_bus_OUT, C_bus_OUT, Serial_OUT, A_bus_OUT, D_Address_OUT
  UC1 uc1_1 (
    .Serial_IN(pipeline_register_2_serial_out), .DAddress_IN(pipeline_register_2_d_address_out),
    .ALUEnable(UC1_ALU_EN), .LoadStoreEnable(UC1_LS_EN), .Serial_ALU_OUT(UC1_ALU_SD),
    .Serial_Load_OUT(UC1_LS_SD), .DAddress_ALU_OUT(UC1_ALU_DADRES), .DAddress_Load_OUT(UC1_LS_DADRES));  // open: HOLD
  not not_3 (not_3_out, UC1_LS_EN);
  DipSwitch #(.number(2)) dipswitch_1 (.sw1(dipswitch_1_sw1));  // open: sw2
  Register #(.width(16)) BusA_LS (.D(16'haaaa), .en(UC1_LS_EN), .clk(CLK2));  // open: Q, clr
  ClockGenerator clocks (.Auto(dipswitch_1_sw1), .ManualCLK(in_1), .CLK(CLK), .CLK2(CLK2), .CLK3(CLK3), .CLK4(CLK4));
  Pipeline_register LoadStore (
    .S_low_P_high(1'b0), .CLK(CLK3), .Serial_IN(UC1_LS_SD), .D_Address_IN(UC1_LS_DADRES), .Hold(not_3_out),
    .ALUC_OUT(LoadStore_aluc_out), .SH_OUT(LoadStore_sh_out), .Kmx_OUT(LoadStore_kmx_out),
    .MRyMB_OUT(LoadStore_mrymb_out), .B_bus_OUT(LoadStore_b_bus_out), .T_bus_OUT(LoadStore_t_bus_out),
    .C_bus_OUT(LoadStore_c_bus_out), .A_bus_OUT(LoadStore_a_bus_out), .D_Address_OUT(LoadStore_d_address_out));  // open: ALUC_IN, SH_IN, Kmx_IN, MRyMB_IN, B_bus_IN, T_bus_IN, C_bus_IN, A_bus_IN, Serial_OUT
  // Data data_1: pin names not known
  // Probe on LoadStore_aluc_out
  // Probe on LoadStore_sh_out
  // Probe on LoadStore_kmx_out
  // Probe on LoadStore_mrymb_out
  // Probe on LoadStore_b_bus_out
  // Probe on LoadStore_t_bus_out
  // Probe on LoadStore_c_bus_out
  // Probe on LoadStore_a_bus_out
  // Probe on LoadStore_d_address_out

  // Other names for the same wires on the sheet: pulseGenManual = in_1

  // Notes on the sheet:
  //   contents of ProgramMemory (hex, n*v repeats v):
  //   400140 9*0 600040
  //   BUS B
endmodule
